// Logisim project projeto3.circ as structural Verilog: 8 circuits, main circuit Trabalho
module Trabalho (
  input  Habilitador,
  input  CLEAR,
  input  PRESET,
  input  CONTROLE,
  input  CONTROLE_2
);

  wire and_1_out, and_2_out, and_3_out, and_4_out, CLEAR_out, clock_1_out, decodificador_hexadecimal_1_a_2,
       decodificador_hexadecimal_1_b_2, decodificador_hexadecimal_1_c_2, decodificador_hexadecimal_1_d_2,
       decodificador_hexadecimal_1_e, decodificador_hexadecimal_1_f, decodificador_hexadecimal_1_g,
       decodificador_hexadecimal_2_a_2, decodificador_hexadecimal_2_b_2, decodificador_hexadecimal_2_c_2,
       decodificador_hexadecimal_2_d_2, decodificador_hexadecimal_2_e, decodificador_hexadecimal_2_f,
       decodificador_hexadecimal_2_g, decodificador_hexadecimal_3_a_2, decodificador_hexadecimal_3_b_2,
       decodificador_hexadecimal_3_c_2, decodificador_hexadecimal_3_d_2, decodificador_hexadecimal_3_e,
       decodificador_hexadecimal_3_f, decodificador_hexadecimal_3_g, j_k_ff_1_q, j_k_ff_2_q, j_k_ff_3_q,
       j_k_ff_3_qn, j_k_ff_4_q, not_1_out, not_2_out, not_3_out, not_4_out, not_5_out, not_6_out, not_7_out,
       not_8_out, not_9_out, not_10_out, not_11_out, or_1_out, or_2_out, registrador_1_out_7,
       registrador_1_out_8, registrador_1_out_9, registrador_1_out_10, registrador_2_out_7,
       registrador_2_out_8, registrador_2_out_9, registrador_2_out_10;

  Button u_CLEAR (.out(CLEAR_out));
  and and_1 (and_1_out, j_k_ff_2_q, j_k_ff_3_q, j_k_ff_4_q);
  Clock clock_1 (.out(clock_1_out));
  J_K_Flip_Flop j_k_ff_1 (
    .J(and_1_out), .clk(clock_1_out), .K(1'b1), .Q(j_k_ff_1_q), .preset(not_2_out), .en(Habilitador),
    .reset(not_1_out));  // open: Qn
  not not_1 (not_1_out, CLEAR);
  not not_2 (not_2_out, PRESET);
  not not_3 (not_3_out, j_k_ff_3_q);
  and and_2 (and_2_out, clock_1_out, CONTROLE);
  J_K_Flip_Flop j_k_ff_2 (
    .J(1'b1), .clk(clock_1_out), .K(or_1_out), .Q(j_k_ff_2_q), .preset(not_5_out), .en(Habilitador),
    .reset(not_4_out));  // open: Qn
  or or_1 (or_1_out, not_3_out, j_k_ff_4_q);
  not not_4 (not_4_out, CLEAR);
  not not_5 (not_5_out, PRESET);
  REGISTRADOR registrador_1 (
    .in_2(j_k_ff_1_q), .in_3(j_k_ff_2_q), .in_4(j_k_ff_3_q), .in_5(j_k_ff_4_q), .CLOCK(and_2_out),
    .CLEAR(CLEAR_out), .out_7(registrador_1_out_7), .out_8(registrador_1_out_8), .out_9(registrador_1_out_9),
    .out_10(registrador_1_out_10));
  not not_6 (not_6_out, j_k_ff_4_q);
  or or_2 (or_2_out, not_6_out, j_k_ff_2_q);
  not not_7 (not_7_out, CLEAR);
  not not_8 (not_8_out, PRESET);
  Decodificador_Hexadecimal decodificador_hexadecimal_1 (
    .A(registrador_1_out_7), .B(registrador_1_out_8), .C(registrador_1_out_9), .D(registrador_1_out_10),
    .a_2(decodificador_hexadecimal_1_a_2), .b_2(decodificador_hexadecimal_1_b_2),
    .c_2(decodificador_hexadecimal_1_c_2), .d_2(decodificador_hexadecimal_1_d_2),
    .e(decodificador_hexadecimal_1_e), .f(decodificador_hexadecimal_1_f), .g(decodificador_hexadecimal_1_g));
  _7_Segment_Display u_7_segment_display_1 (
    .g(decodificador_hexadecimal_1_g), .f(decodificador_hexadecimal_1_f),
    .a(decodificador_hexadecimal_1_a_2), .b(decodificador_hexadecimal_1_b_2),
    .e(decodificador_hexadecimal_1_e), .d(decodificador_hexadecimal_1_d_2),
    .c(decodificador_hexadecimal_1_c_2));  // open: dp
  not not_9 (not_9_out, j_k_ff_2_q);
  J_K_Flip_Flop j_k_ff_3 (
    .J(1'b1), .clk(clock_1_out), .K(or_2_out), .Q(j_k_ff_3_q), .Qn(j_k_ff_3_qn), .preset(not_8_out),
    .en(Habilitador), .reset(not_7_out));
  and and_3 (and_3_out, not_9_out, j_k_ff_3_qn);
  not not_10 (not_10_out, CLEAR);
  not not_11 (not_11_out, PRESET);
  J_K_Flip_Flop j_k_ff_4 (
    .J(not_9_out), .clk(clock_1_out), .K(and_3_out), .Q(j_k_ff_4_q), .preset(not_11_out), .en(Habilitador),
    .reset(not_10_out));  // open: Qn
  Decodificador_Hexadecimal decodificador_hexadecimal_2 (
    .A(j_k_ff_1_q), .B(j_k_ff_2_q), .C(j_k_ff_3_q), .D(j_k_ff_4_q), .a_2(decodificador_hexadecimal_2_a_2),
    .b_2(decodificador_hexadecimal_2_b_2), .c_2(decodificador_hexadecimal_2_c_2),
    .d_2(decodificador_hexadecimal_2_d_2), .e(decodificador_hexadecimal_2_e),
    .f(decodificador_hexadecimal_2_f), .g(decodificador_hexadecimal_2_g));
  and and_4 (and_4_out, clock_1_out, CONTROLE_2);
  REGISTRADOR registrador_2 (
    .in_2(j_k_ff_1_q), .in_3(j_k_ff_2_q), .in_4(j_k_ff_3_q), .in_5(j_k_ff_4_q), .CLOCK(and_4_out),
    .CLEAR(CLEAR_out), .out_7(registrador_2_out_7), .out_8(registrador_2_out_8), .out_9(registrador_2_out_9),
    .out_10(registrador_2_out_10));
  _7_Segment_Display u_7_segment_display_2 (
    .g(decodificador_hexadecimal_2_g), .f(decodificador_hexadecimal_2_f),
    .a(decodificador_hexadecimal_2_a_2), .b(decodificador_hexadecimal_2_b_2),
    .e(decodificador_hexadecimal_2_e), .d(decodificador_hexadecimal_2_d_2),
    .c(decodificador_hexadecimal_2_c_2));  // open: dp
  Decodificador_Hexadecimal decodificador_hexadecimal_3 (
    .A(registrador_2_out_7), .B(registrador_2_out_8), .C(registrador_2_out_9), .D(registrador_2_out_10),
    .a_2(decodificador_hexadecimal_3_a_2), .b_2(decodificador_hexadecimal_3_b_2),
    .c_2(decodificador_hexadecimal_3_c_2), .d_2(decodificador_hexadecimal_3_d_2),
    .e(decodificador_hexadecimal_3_e), .f(decodificador_hexadecimal_3_f), .g(decodificador_hexadecimal_3_g));
  _7_Segment_Display u_7_segment_display_3 (
    .g(decodificador_hexadecimal_3_g), .f(decodificador_hexadecimal_3_f),
    .a(decodificador_hexadecimal_3_a_2), .b(decodificador_hexadecimal_3_b_2),
    .e(decodificador_hexadecimal_3_e), .d(decodificador_hexadecimal_3_d_2),
    .c(decodificador_hexadecimal_3_c_2));  // open: dp

  // Notes on the sheet:
  //   Q3
  //   Q2
  //   Q1
  //   Q0
endmodule

// DECODE
module Decodificador_Hexadecimal (
  input  A,
  input  B,
  input  C,
  input  D,
  output a_2,
  output b_2,
  output c_2,
  output d_2,
  output e,
  output f,
  output g
);

  wire and_1_out, and_2_out, and_3_out, and_4_out, and_5_out, and_6_out, and_7_out, and_8_out, and_9_out,
       and_10_out, and_11_out, and_12_out, and_13_out, and_14_out, and_15_out, and_16_out, and_17_out,
       and_18_out, and_19_out, and_20_out, and_21_out, and_22_out, and_23_out, and_24_out, and_25_out,
       and_26_out, and_27_out, and_28_out, and_29_out, and_30_out, and_31_out, and_32_out, and_33_out,
       and_34_out, and_35_out, not_1_out, not_2_out, not_3_out, not_4_out, not_5_out, not_6_out, not_7_out,
       not_8_out, not_9_out, not_10_out, not_11_out, not_12_out, not_13_out, not_14_out, not_15_out,
       not_16_out, not_17_out, not_18_out, not_19_out, not_20_out, not_21_out, not_22_out, not_23_out,
       not_24_out, not_25_out, not_26_out, not_27_out, not_28_out, not_29_out, not_30_out, not_31_out,
       not_32_out, not_33_out, not_34_out, not_35_out, not_36_out, not_37_out, not_38_out, not_39_out,
       not_40_out, not_41_out, not_42_out, not_43_out;

  not not_1 (not_1_out, B);
  and and_1 (and_1_out, not_1_out, not_2_out);
  not not_2 (not_2_out, D);
  not not_3 (not_3_out, A);
  and and_2 (and_2_out, not_3_out, C);
  not not_4 (not_4_out, A);
  and and_3 (and_3_out, not_4_out, B, D);
  and and_4 (and_4_out, B, C);
  not not_5 (not_5_out, B);
  and and_5 (and_5_out, A, not_5_out, not_6_out);
  not not_6 (not_6_out, C);
  and and_6 (and_6_out, A, not_7_out);
  not not_7 (not_7_out, D);
  not not_8 (not_8_out, A);
  and and_7 (and_7_out, not_8_out, not_9_out);
  not not_9 (not_9_out, B);
  not not_10 (not_10_out, A);
  not not_11 (not_11_out, C);
  and and_8 (and_8_out, not_10_out, not_11_out, not_12_out);
  not not_12 (not_12_out, D);
  not not_13 (not_13_out, B);
  and and_9 (and_9_out, not_13_out, not_14_out);
  not not_14 (not_14_out, D);
  not not_15 (not_15_out, A);
  and and_10 (and_10_out, not_15_out, C, D);
  and and_11 (and_11_out, A, not_16_out, D);
  not not_16 (not_16_out, C);
  not not_17 (not_17_out, A);
  and and_12 (and_12_out, not_17_out, not_18_out);
  not not_18 (not_18_out, C);
  not not_19 (not_19_out, A);
  and and_13 (and_13_out, not_19_out, D);
  not not_20 (not_20_out, C);
  and and_14 (and_14_out, not_20_out, D);
  not not_21 (not_21_out, A);
  and and_15 (and_15_out, not_21_out, B);
  and and_16 (and_16_out, A, not_22_out);
  not not_22 (not_22_out, B);
  not not_23 (not_23_out, A);
  and and_17 (and_17_out, not_23_out, not_24_out, not_25_out);
  not not_24 (not_24_out, B);
  not not_25 (not_25_out, D);
  not not_26 (not_26_out, B);
  and and_18 (and_18_out, not_26_out, C, D);
  not not_27 (not_27_out, C);
  and and_19 (and_19_out, B, not_27_out, D);
  and and_20 (and_20_out, B, C, not_28_out);
  not not_28 (not_28_out, D);
  and and_21 (and_21_out, A, not_29_out);
  not not_29 (not_29_out, C);
  not not_30 (not_30_out, B);
  and and_22 (and_22_out, not_30_out, not_31_out);
  not not_31 (not_31_out, D);
  and and_23 (and_23_out, C, not_32_out);
  not not_32 (not_32_out, D);
  and and_24 (and_24_out, A, C);
  and and_25 (and_25_out, A, B);
  not not_33 (not_33_out, C);
  and and_26 (and_26_out, not_33_out, not_34_out);
  not not_34 (not_34_out, D);
  not not_35 (not_35_out, A);
  and and_27 (and_27_out, not_35_out, B, not_36_out);
  not not_36 (not_36_out, C);
  and and_28 (and_28_out, B, not_37_out);
  not not_37 (not_37_out, D);
  and and_29 (and_29_out, A, not_38_out);
  not not_38 (not_38_out, B);
  and and_30 (and_30_out, A, C);
  not not_39 (not_39_out, B);
  and and_31 (and_31_out, not_39_out, C);
  and and_32 (and_32_out, C, not_40_out);
  not not_40 (not_40_out, D);
  not not_41 (not_41_out, A);
  and and_33 (and_33_out, not_41_out, B, not_42_out);
  not not_42 (not_42_out, C);
  and and_34 (and_34_out, A, not_43_out);
  not not_43 (not_43_out, B);
  and and_35 (and_35_out, A, D);
  or or_1 (b_2, and_7_out, and_8_out, and_9_out, and_10_out, and_11_out);
  or or_2 (c_2, and_12_out, and_13_out, and_14_out, and_15_out, and_16_out);
  or or_3 (d_2, and_17_out, and_18_out, and_19_out, and_20_out, and_21_out);
  or or_4 (e, and_22_out, and_23_out, and_24_out, and_25_out);
  or or_5 (f, and_26_out, and_27_out, and_28_out, and_29_out, and_30_out);
  or or_6 (g, and_31_out, and_32_out, and_33_out, and_34_out, and_35_out);
  or or_7 (a_2, and_1_out, and_2_out, and_3_out, and_4_out, and_5_out, and_6_out);
endmodule

// REG
module REGISTRADOR (
  input  CLOCK,
  input  in_2,
  input  in_3,
  input  in_4,
  input  in_5,
  input  CLEAR,
  output out_7,
  output out_8,
  output out_9,
  output out_10
);

  wire undriven, undriven_2;

  Register #(.width(1)) register_1 (.D(in_2), .en(undriven), .Q(out_7), .clk(CLOCK), .clr(CLEAR));
  Register #(.width(1)) register_2 (.D(in_3), .en(undriven), .Q(out_8), .clk(CLOCK), .clr(CLEAR));
  Register #(.width(1)) register_3 (.D(in_4), .en(undriven_2), .Q(out_9), .clk(CLOCK), .clr(CLEAR));
  Register #(.width(1)) register_4 (.D(in_5), .en(undriven_2), .Q(out_10), .clk(CLOCK), .clr(CLEAR));
endmodule

module J3 (
  input  Q2,
  input  Q1,
  input  Q0,
  output J3
);

  and and_1 (J3, Q1, Q2, Q0);
endmodule

module K2 (
  input  Q1,
  input  Q0,
  output K2
);

  wire not_1_out;

  not not_1 (not_1_out, Q1);
  or or_1 (K2, not_1_out, Q0);
endmodule

module K1 (
  input  Q2,
  input  Q0,
  output K1
);

  wire not_1_out;

  not not_1 (not_1_out, Q0);
  or or_1 (K1, not_1_out, Q2);
endmodule

module J0 (
  input  Q2,
  output J0
);

  not not_1 (J0, Q2);
endmodule

module K0 (
  input  Q2,
  input  Q1,
  output K0
);

  wire not_1_out, not_2_out;

  not not_1 (not_1_out, Q2);
  and and_1 (K0, not_1_out, not_2_out);
  not not_2 (not_2_out, Q1);
endmodule
